// Logisim project ALU.circ as structural Verilog: 18 circuits, main circuit adder8
module main (
  input  [31:0] A,
  input  [31:0] B,
  input  [4:0] Sa,
  input  [3:0] Op,
  output V,
  output [31:0] C
);

  ALU32 alu32_1 (.A(A), .B(B), .Sa(Sa), .Op(Op), .V(V), .C(C));
endmodule

module XOR (
  input  in_1,
  input  in_2,
  output out_3
);

  wire and_1_out, and_2_out, not_1_out, not_2_out;

  not not_1 (not_1_out, in_1);
  not not_2 (not_2_out, in_2);
  and and_1 (and_1_out, not_1_out, in_2);
  and and_2 (and_2_out, in_1, not_2_out);
  or or_1 (out_3, and_1_out, and_2_out);
endmodule

module Adder (
  input  A,
  input  B,
  input  Cin,
  output S,
  output Cout
);

  wire and_1_out, and_2_out, xor_1_out_3;

  XOR xor_1 (.in_1(A), .in_2(B), .out_3(xor_1_out_3));
  and and_1 (and_1_out, A, B);
  XOR xor_2 (.in_1(xor_1_out_3), .in_2(Cin), .out_3(S));
  and and_2 (and_2_out, xor_1_out_3, Cin);
  or or_1 (Cout, and_2_out, and_1_out);
endmodule

module _4bitadder (
  input  C,
  input  [3:0] A,
  input  [3:0] B,
  output [3:0] S,
  output C4
);

  wire adder_1_cout, adder_2_cout, adder_3_cout;

  Adder adder_1 (.A(C), .B(A[0]), .Cin(B[0]), .S(S[0]), .Cout(adder_1_cout));
  Adder adder_2 (.A(adder_1_cout), .B(A[1]), .Cin(B[1]), .S(S[1]), .Cout(adder_2_cout));
  Adder adder_3 (.A(adder_2_cout), .B(A[2]), .Cin(B[2]), .S(S[2]), .Cout(adder_3_cout));
  Adder adder_4 (.A(adder_3_cout), .B(A[3]), .Cin(B[3]), .S(S[3]), .Cout(C4));
endmodule

module adder8 (
  input  C,
  input  [7:0] A,
  input  [7:0] B,
  output [7:0] S,
  output C8
);

  wire n4bitadder_1_c4;

  _4bitadder u_4bitadder_1 (.C(C), .A(A[3:0]), .B(B[3:0]), .S(S[3:0]), .C4(n4bitadder_1_c4));
  _4bitadder u_4bitadder_2 (.C(n4bitadder_1_c4), .A(A[7:4]), .B(B[7:4]), .S(S[7:4]), .C4(C8));
endmodule

module _4bit_with_overflow (
  input  C,
  input  [3:0] A,
  input  [3:0] B,
  output [3:0] S,
  output V
);

  wire adder_1_cout, adder_2_cout, adder_3_cout, adder_4_cout;

  Adder adder_1 (.A(C), .B(A[0]), .Cin(B[0]), .S(S[0]), .Cout(adder_1_cout));
  Adder adder_2 (.A(adder_1_cout), .B(A[1]), .Cin(B[1]), .S(S[1]), .Cout(adder_2_cout));
  Adder adder_3 (.A(adder_2_cout), .B(A[2]), .Cin(B[2]), .S(S[2]), .Cout(adder_3_cout));
  Adder adder_4 (.A(adder_3_cout), .B(A[3]), .Cin(B[3]), .S(S[3]), .Cout(adder_4_cout));
  xor xor_1 (V, adder_3_cout, adder_4_cout);
endmodule

module _8bit_with_overflow (
  input  C,
  input  [7:0] A,
  input  [7:0] A_2,
  output [7:0] S,
  output V8
);

  wire n4bitadder_1_c4;

  _4bitadder u_4bitadder_1 (.C(C), .A(A[3:0]), .B(A_2[3:0]), .S(S[3:0]), .C4(n4bitadder_1_c4));
  _4bit_with_overflow u_4bit_with_overflow_1 (.C(n4bitadder_1_c4), .A(A[7:4]), .B(A_2[7:4]), .S(S[7:4]), .V(V8));
endmodule

module add_subtract32 (
  input  [31:0] in_1,
  input  [31:0] in_2,
  input  in_3,
  output [31:0] out_4,
  output out_5
);

  wire [31:0] multiplexer_1_out, not_1_out;

  assign not_1_out = ~in_2;  // NOT_Gate not_1, 32 bits wide
  Multiplexer #(.width(32)) multiplexer_1 (
    .in0(in_2), .in1(not_1_out), .out(multiplexer_1_out), .sel(in_3));  // open: en
  Add32 add32_1 (.Cin(in_3), .A(in_1), .B(multiplexer_1_out), .C(out_4), .V(out_5));
endmodule

module reverser32 (
  input  [31:0] In,
  output [31:0] out_2
);


  assign out_2 = {In[0], In[1], In[2], In[3], In[4], In[5], In[6], In[7], In[8], In[9], In[10], In[11], In[12], In[13], In[14], In[15], In[16], In[17], In[18], In[19], In[20], In[21], In[22], In[23], In[24], In[25], In[26], In[27], In[28], In[29], In[30], In[31]};
endmodule

module Eq32 (
  input  [31:0] in_1,
  output out_2
);

  nor nor_1 (out_2, in_1[0], in_1[1], in_1[2], in_1[3], in_1[4], in_1[5], in_1[6], in_1[7], in_1[8], in_1[9], in_1[10], in_1[11], in_1[12], in_1[13], in_1[14], in_1[15], in_1[16], in_1[17], in_1[18], in_1[19], in_1[20], in_1[21], in_1[22], in_1[23], in_1[24], in_1[25], in_1[26], in_1[27], in_1[28], in_1[29], in_1[30], in_1[31]);
endmodule

module LeftShift1 (
  input  [31:0] B,
  input  Cin,
  input  Sa,
  output [31:0] out_4
);

  Multiplexer #(.width(32), .enable("false")) multiplexer_1 (.in0(B), .in1({B[30:0], Cin}), .out(out_4), .sel(Sa));
endmodule

module LeftShift2 (
  input  [31:0] B,
  input  Cin,
  input  Sa,
  output [31:0] out_4
);

  Multiplexer #(.width(32), .enable("false")) multiplexer_1 (.in0(B), .in1({B[29:0], {2{Cin}}}), .out(out_4), .sel(Sa));
endmodule

module LeftShift4 (
  input  [31:0] B,
  input  Cin,
  input  Sa,
  output [31:0] out_4
);

  Multiplexer #(.width(32), .enable("false")) multiplexer_1 (.in0(B), .in1({B[27:0], {4{Cin}}}), .out(out_4), .sel(Sa));
endmodule

module LeftShift8 (
  input  [31:0] in_1,
  input  Cin,
  input  Sa,
  output [31:0] out_4
);

  Multiplexer #(.width(32), .enable("false")) multiplexer_1 (
    .in0(in_1), .in1({in_1[23:0], {8{Cin}}}), .out(out_4), .sel(Sa));
endmodule

module LeftShift16 (
  input  [31:0] B,
  input  Cin,
  input  in_3,
  output [31:0] out_4
);

  Multiplexer #(.width(32), .enable("false")) multiplexer_1 (
    .in0(B), .in1({B[15:0], {16{Cin}}}), .out(out_4), .sel(in_3));
endmodule

module LeftShift32 (
  input  [31:0] B,
  input  Cin,
  input  [4:0] Sa,
  output [31:0] C
);

  wire [31:0] leftshift2_1_out_4, leftshift4_1_out_4, leftshift8_1_out_4, leftshift16_1_out_4;

  LeftShift16 leftshift16_1 (.B(B), .Cin(Cin), .in_3(Sa[4]), .out_4(leftshift16_1_out_4));
  LeftShift8 leftshift8_1 (.in_1(leftshift16_1_out_4), .Cin(Cin), .Sa(Sa[3]), .out_4(leftshift8_1_out_4));
  LeftShift4 leftshift4_1 (.B(leftshift8_1_out_4), .Cin(Cin), .Sa(Sa[2]), .out_4(leftshift4_1_out_4));
  LeftShift2 leftshift2_1 (.B(leftshift4_1_out_4), .Cin(Cin), .Sa(Sa[1]), .out_4(leftshift2_1_out_4));
  LeftShift1 leftshift1_1 (.B(leftshift2_1_out_4), .Cin(Cin), .Sa(Sa[0]), .out_4(C));
endmodule

module Add32 (
  input  Cin,
  input  [31:0] A,
  input  [31:0] B,
  output [31:0] C,
  output V
);

  wire adder8_1_c8, adder8_2_c8, adder8_3_c8;

  adder8 adder8_1 (.C(Cin), .A(A[7:0]), .B(B[7:0]), .S(C[7:0]), .C8(adder8_1_c8));
  adder8 adder8_2 (.C(adder8_1_c8), .A(A[15:8]), .B(B[15:8]), .S(C[15:8]), .C8(adder8_2_c8));
  adder8 adder8_3 (.C(adder8_2_c8), .A(A[23:16]), .B(B[23:16]), .S(C[23:16]), .C8(adder8_3_c8));
  _8bit_with_overflow u_8bit_with_overflow_1 (.C(adder8_3_c8), .A(A[31:24]), .A_2(B[31:24]), .S(C[31:24]), .V8(V));
endmodule

module ALU32 (
  input  [31:0] A,
  input  [31:0] B,
  input  [4:0] Sa,
  input  [3:0] Op,
  output V,
  output [31:0] C
);

  wire add_subtract32_1_out_5, and_2_out, and_3_out, and_4_out, eq32_1_out_2, eq32_2_out_2,
       multiplexer_3_out, multiplexer_4_out, not_2_out, not_3_out, not_4_out, not_5_out, or_2_out, or_3_out;
  wire [31:0] add_subtract32_1_out_4, and_1_out, bit_extender_1_out, bit_extender_2_out, bit_extender_3_out,
       leftshift32_1_c, multiplexer_1_out, multiplexer_2_out, not_1_out, or_1_out, reverser32_1_out_2,
       reverser32_2_out_2, xor_1_out;

  assign and_1_out = A & B;  // AND_Gate and_1, 32 bits wide
  assign or_1_out = A | B;  // OR_Gate or_1, 32 bits wide
  assign xor_1_out = A ^ B;  // XOR_Gate xor_1, 32 bits wide
  or or_2 (or_2_out, Op[3], Op[2]);
  reverser32 reverser32_1 (.In(A), .out_2(reverser32_1_out_2));
  assign not_1_out = ~or_1_out;  // NOT_Gate not_1, 32 bits wide
  Multiplexer #(.width(32)) multiplexer_1 (
    .in0(A), .in1(reverser32_1_out_2), .out(multiplexer_1_out), .sel(Op[2]));  // open: en
  LeftShift32 leftshift32_1 (.B(multiplexer_1_out), .Cin(and_2_out), .Sa(Sa), .C(leftshift32_1_c));
  and and_2 (and_2_out, A[31], Op[0]);
  and and_3 (and_3_out, Op[1], not_2_out);
  not not_2 (not_2_out, Op[3]);
  add_subtract32 add_subtract32_1 (
    .in_1(A), .in_2(B), .in_3(or_2_out), .out_4(add_subtract32_1_out_4), .out_5(add_subtract32_1_out_5));
  reverser32 reverser32_2 (.In(leftshift32_1_c), .out_2(reverser32_2_out_2));
  Multiplexer #(.width(32)) multiplexer_2 (
    .in0(leftshift32_1_c), .in1(reverser32_2_out_2), .out(multiplexer_2_out), .sel(Op[2]));  // open: en
  Eq32 eq32_1 (.in_1(add_subtract32_1_out_4), .out_2(eq32_1_out_2));
  not not_3 (not_3_out, eq32_1_out_2);
  assign bit_extender_1_out = {{1{1'b0}}, add_subtract32_1_out_4[30:0]};  // Bit_Extender bit_extender_1
  Eq32 eq32_2 (.in_1(bit_extender_1_out), .out_2(eq32_2_out_2));
  not not_4 (not_4_out, add_subtract32_1_out_4[31]);
  Multiplexer multiplexer_3 (.in0(eq32_1_out_2), .in1(not_3_out), .out(multiplexer_3_out), .sel(Op[1]));  // open: en
  not not_5 (not_5_out, eq32_2_out_2);
  and and_4 (and_4_out, not_5_out, not_4_out);
  or or_3 (or_3_out, eq32_2_out_2, add_subtract32_1_out_4[31]);
  assign bit_extender_2_out = {{31{1'b0}}, multiplexer_3_out};  // Bit_Extender bit_extender_2
  Multiplexer multiplexer_4 (.in0(and_4_out), .in1(or_3_out), .out(multiplexer_4_out), .sel(Op[1]));  // open: en
  and and_5 (V, add_subtract32_1_out_5, and_3_out);
  Multiplexer #(.select(4), .width(32)) multiplexer_5 (
    .in0(multiplexer_2_out), .in1(multiplexer_2_out), .in2(add_subtract32_1_out_4),
    .in3(add_subtract32_1_out_4), .in4(multiplexer_2_out), .in5(multiplexer_2_out),
    .in6(add_subtract32_1_out_4), .in7(add_subtract32_1_out_4), .in8(and_1_out), .in9(bit_extender_2_out),
    .in10(or_1_out), .in11(bit_extender_2_out), .in12(xor_1_out), .in13(bit_extender_3_out),
    .in14(not_1_out), .in15(bit_extender_3_out), .out(C), .sel(Op));  // open: en
  assign bit_extender_3_out = {{31{1'b0}}, multiplexer_4_out};  // Bit_Extender bit_extender_3
endmodule
