// Logisim project mips.circ as structural Verilog: 16 circuits, main circuit main
module main (
);

  wire clock_1_out;
  wire [1:0] ex_1_decide;
  wire [4:0] ex_1_ra_2, ex_1_rb_2, ex_1_rw_2, ex_mem_1_rw_2, id_1_ra, id_1_rb, id_1_rw_2, id_1_sa,
       id_ex_1_ra_2, id_ex_1_rb_2, id_ex_1_rw_2, id_ex_1_sa_2, mem_wb_1_rw_2;
  wire [5:0] ex_1_op_2, ex_mem_1_op_2, id_1_f, id_1_op, id_ex_1_f_2, id_ex_1_op_2, mem_1_op_2;
  wire [31:0] ex_1_d, ex_1_m, ex_1_pcabs, ex_1_pcreg, ex_1_pcrel, ex_mem_1_d_2, ex_mem_1_m_2, forwarding_1_a,
       forwarding_1_b, id_1_a, id_1_b, id_1_imm, id_ex_1_a_2, id_ex_1_b_2, id_ex_1_imm_2, id_ex_1_pc_2,
       if_1_inst, if_1_pc_4, if_id_1_inst_2, if_id_1_pc_2, mem_1_d_2, mem_1_m_2, mem_wb_1_d_2;

  Clock clock_1 (.out(clock_1_out));
  IF if_1 (
    .DECIDE(ex_1_decide), .PC1(ex_1_pcrel), .PC2(ex_1_pcreg), .PC3(ex_1_pcabs), .CLOCK(clock_1_out),
    .INST(if_1_inst), .PC_4(if_1_pc_4));
  IF_ID if_id_1 (.INST(if_1_inst), .PC(if_1_pc_4), .CLOCK(clock_1_out), .INST_2(if_id_1_inst_2), .PC_2(if_id_1_pc_2));
  ID id_1 (
    .WB(mem_wb_1_d_2), .INST(if_id_1_inst_2), .RW(mem_wb_1_rw_2), .CLOCK(clock_1_out), .A(id_1_a),
    .B(id_1_b), .IMM(id_1_imm), .OP(id_1_op), .RW_2(id_1_rw_2), .RA(id_1_ra), .RB(id_1_rb), .SA(id_1_sa),
    .F(id_1_f));
  Forwarding forwarding_1 (
    .A_Current(id_1_a), .B_Current(id_1_b), .Post_ALU_Value(ex_1_d), .Post_Mem_Value(mem_1_d_2),
    .Register_for_A(id_1_ra), .Post_Alu(ex_1_rw_2), .Post_Mem(ex_mem_1_rw_2), .Register_for_B(id_1_rb),
    .A(forwarding_1_a), .B(forwarding_1_b));
  ID_EX id_ex_1 (
    .A(forwarding_1_a), .B(forwarding_1_b), .IMM(id_1_imm), .OP(id_1_op), .RW(id_1_rw_2), .RA(id_1_ra),
    .RB(id_1_rb), .SA(id_1_sa), .F(id_1_f), .PC(if_id_1_pc_2), .CLOCK(clock_1_out), .A_2(id_ex_1_a_2),
    .B_2(id_ex_1_b_2), .IMM_2(id_ex_1_imm_2), .OP_2(id_ex_1_op_2), .RW_2(id_ex_1_rw_2), .RA_2(id_ex_1_ra_2),
    .RB_2(id_ex_1_rb_2), .SA_2(id_ex_1_sa_2), .F_2(id_ex_1_f_2), .PC_2(id_ex_1_pc_2));
  EX ex_1 (
    .A(id_ex_1_a_2), .B(id_ex_1_b_2), .IMM(id_ex_1_imm_2), .OP(id_ex_1_op_2), .RW(id_ex_1_rw_2),
    .RA(id_ex_1_ra_2), .RB(id_ex_1_rb_2), .SA(id_ex_1_sa_2), .F(id_ex_1_f_2), .PC_4(id_ex_1_pc_2),
    .D(ex_1_d), .M(ex_1_m), .OP_2(ex_1_op_2), .RW_2(ex_1_rw_2), .RA_2(ex_1_ra_2), .RB_2(ex_1_rb_2),
    .PCREL(ex_1_pcrel), .PCREG(ex_1_pcreg), .PCABS(ex_1_pcabs), .DECIDE(ex_1_decide));
  EX_MEM ex_mem_1 (
    .D(ex_1_d), .M(ex_1_m), .OP(ex_1_op_2), .RW(ex_1_rw_2), .RA(ex_1_ra_2), .RB(ex_1_rb_2),
    .CLOCK(clock_1_out), .D_2(ex_mem_1_d_2), .M_2(ex_mem_1_m_2), .OP_2(ex_mem_1_op_2), .RW_2(ex_mem_1_rw_2));  // open: RB_2, RA_2
  MEM mem_1 (
    .D(ex_mem_1_d_2), .M(ex_mem_1_m_2), .OP(ex_mem_1_op_2), .CLOCK(clock_1_out), .D_2(mem_1_d_2),
    .M_2(mem_1_m_2), .OP_2(mem_1_op_2));
  MEM_WB mem_wb_1 (
    .D(mem_1_d_2), .M(mem_1_m_2), .OP(mem_1_op_2), .RW(ex_mem_1_rw_2), .CLOCK(clock_1_out),
    .D_2(mem_wb_1_d_2), .RW_2(mem_wb_1_rw_2));  // open: M_2, OP_2
endmodule

module IF (
  input  CLOCK,
  input  [1:0] DECIDE,
  input  [31:0] PC1,
  input  [31:0] PC2,
  input  [31:0] PC3,
  output [31:0] INST,
  output [31:0] PC_4
);

  wire [31:0] multiplexer_1_out, register_1_q;

  Register #(.width(32)) register_1 (.D(multiplexer_1_out), .Q(register_1_q), .clk(CLOCK));  // open: en, clr
  _4 u_4_1 (.IN(register_1_q), .OUT(PC_4));
  Multiplexer #(.select(2), .width(32), .enable("false")) multiplexer_1 (
    .in0(PC_4), .in1(PC3), .in2(PC2), .in3(PC1), .out(multiplexer_1_out), .sel(DECIDE));
  // MIPSProgramROM mipsprogramrom_1: pin names not known; wires that end beside it: register_1_q, INST
endmodule

module ID (
  input  [31:0] WB,
  input  [31:0] INST,
  input  CLOCK,
  input  [4:0] RW,
  output [31:0] A,
  output [31:0] B,
  output [31:0] IMM,
  output [5:0] OP,
  output [4:0] RW_2,
  output [4:0] RA,
  output [4:0] RB,
  output [4:0] SA,
  output [5:0] F
);

  wire and_1_out, not_1_out;

  not not_1 (not_1_out, CLOCK);
  Decode decode_1 (.INST(INST), .OP(OP), .W(RW_2), .A(RA), .B(RB), .SA(SA), .F(F));
  and and_1 (and_1_out, INST[15], ~OP[0]);  // AND_Gate
  // RegisterFile registerfile_1: pin names not known; wires that end beside it: WB, CLOCK, not_1_out, RW, RA, RB, A, B
  assign IMM[31:16] = {{15{and_1_out}}, and_1_out};  // Bit_Extender bit_extender_1

  assign IMM[15:0] = INST[15:0];
endmodule

module EX (
  input  [31:0] A,
  input  [31:0] B,
  input  [31:0] IMM,
  input  [5:0] OP,
  input  [4:0] RW,
  input  [4:0] RA,
  input  [4:0] RB,
  input  [4:0] SA,
  input  [5:0] F,
  input  [31:0] PC_4,
  output [31:0] D,
  output [31:0] M,
  output [5:0] OP_2,
  output [4:0] RW_2,
  output [4:0] RA_2,
  output [4:0] RB_2,
  output [31:0] PCREL,
  output [31:0] PCREG,
  output [31:0] PCABS,
  output [1:0] DECIDE
);

  wire aludecode_1_im, aludecode_1_out_5, and_1_out, and_2_out, and_3_out, and_4_out, nand_1_out, or_2_out;
  wire [3:0] aludecode_1_alu_code;
  wire [4:0] multiplexer_4_out;
  wire [4:4] mips_alu_1_p4;
  wire [31:0] mips_alu_1_p5, multiplexer_1_out, multiplexer_2_out, multiplexer_3_out;

  Multiplexer #(.width(32), .enable("false")) multiplexer_1 (
    .in0(B), .in1(IMM), .out(multiplexer_1_out), .sel(aludecode_1_im));
  ALUDecode aludecode_1 (
    .F(F), .Op(OP), .out_5(aludecode_1_out_5), .ALU_Code(aludecode_1_alu_code), .IM(aludecode_1_im));
  Multiplexer #(.width(32), .enable("false")) multiplexer_2 (
    .in0(A), .in1(multiplexer_1_out), .out(multiplexer_2_out), .sel(and_1_out));
  Multiplexer #(.width(32), .enable("false")) multiplexer_3 (
    .in0(multiplexer_1_out), .in1(A), .out(multiplexer_3_out), .sel(and_1_out));
  and and_1 (and_1_out, aludecode_1_alu_code[0], aludecode_1_alu_code[2], aludecode_1_alu_code[3]);
  and and_2 (and_2_out, ~OP[5], ~OP[4], OP[3], OP[2], OP[1], OP[0]);  // AND_Gate
  Multiplexer #(.width(5), .enable("false")) multiplexer_4 (
    .in0(RA), .in1(SA), .out(multiplexer_4_out), .sel(nand_1_out));
  nand nand_1 (nand_1_out, F[2], ~F[3], ~F[5]);  // NAND_Gate
  // Mips_ALU mips_alu_1: pin names not known; wires that end beside it: multiplexer_2_out, multiplexer_3_out, aludecode_1_alu_code, {mips_alu_1_p4[4], multiplexer_4_out[3:0]}, mips_alu_1_p5
  or or_1 (mips_alu_1_p4[4], multiplexer_4_out[4], and_2_out);
  Multiplexer #(.width(32), .enable("false")) multiplexer_5 (.in0(mips_alu_1_p5), .in1(A), .out(D), .sel(and_3_out));
  and and_3 (and_3_out, and_4_out, aludecode_1_out_5);
  and and_4 (and_4_out, aludecode_1_alu_code[0], ~aludecode_1_alu_code[2], aludecode_1_alu_code[3]);  // AND_Gate
  Adder #(.width(32)) adder_1 (.a(IMM), .b(PC_4), .out(PCREL));  // open: cin, cout
  or or_2 (or_2_out, aludecode_1_im, and_4_out);
  Multiplexer #(.width(5), .enable("false")) multiplexer_6 (.in0(RW), .in1(RB), .out(RW_2), .sel(or_2_out));

  assign DECIDE = 2'b00;
  assign M = B;
  assign OP_2 = OP;
  assign PCABS = {PC_4[31:28], RW, RW, IMM[15:0], 2'b00};
  assign PCREG = A;
  assign RA_2 = RA;
  assign RB_2 = RB;
endmodule

module MEM (
  input  [31:0] D,
  input  [31:0] M,
  input  CLOCK,
  input  [5:0] OP,
  output [31:0] D_2,
  output [31:0] M_2,
  output [5:0] OP_2
);

  Memory2 memory2_1 (.M(M), .D(D), .OP(OP), .CLOCK(CLOCK), .M_2(M_2));

  assign D_2 = D;
  assign OP_2 = OP;
endmodule

module WB (
  input  [31:0] D,
  input  [4:0] RW,
  output [31:0] WB,
  output [4:0] out_4
);


  assign out_4 = RW;
  assign WB = D;
endmodule

module Forwarding (
  input  [31:0] A_Current,
  input  [31:0] B_Current,
  input  [31:0] Post_ALU_Value,
  input  [31:0] Post_Mem_Value,
  input  [4:0] Register_for_A,
  input  [4:0] Post_Alu,
  input  [4:0] Post_Mem,
  input  [4:0] Register_for_B,
  output [31:0] A,
  output [31:0] B
);

  wire and_1_out, and_2_out, and_3_out, and_4_out, and_5_out, and_6_out, and_7_out, and_8_out, and_9_out,
       and_10_out, and_11_out, and_12_out, and_13_out, and_14_out, and_15_out, and_16_out, and_17_out,
       and_18_out, and_19_out, and_20_out, or_1_out, or_2_out, or_3_out, or_4_out, or_5_out, or_6_out;
  wire [1:0] and_22_out, and_24_out;
  wire [4:0] not_1_out, not_2_out, not_3_out, not_4_out;

  or or_1 (or_1_out, Register_for_A[4], Register_for_A[3], Register_for_A[2], Register_for_A[1], Register_for_A[0]);
  assign not_1_out = ~Post_Alu;  // NOT_Gate not_1, 5 bits wide
  assign not_2_out = ~Post_Mem;  // NOT_Gate not_2, 5 bits wide
  or or_2 (or_2_out, Register_for_B[4], Register_for_B[3], Register_for_B[2], Register_for_B[1], Register_for_B[0]);
  assign not_3_out = ~Post_Alu;  // NOT_Gate not_3, 5 bits wide
  assign not_4_out = ~Post_Mem;  // NOT_Gate not_4, 5 bits wide
  and and_1 (and_1_out, Register_for_A[0], not_1_out[0]);
  and and_2 (and_2_out, Register_for_A[1], not_1_out[1]);
  and and_3 (and_3_out, Register_for_A[2], not_1_out[2]);
  and and_4 (and_4_out, Register_for_A[3], not_1_out[3]);
  and and_5 (and_5_out, not_1_out[4], Register_for_A[4]);
  and and_6 (and_6_out, Register_for_A[0], not_2_out[0]);
  and and_7 (and_7_out, Register_for_A[1], not_2_out[1]);
  and and_8 (and_8_out, Register_for_A[2], not_2_out[2]);
  and and_9 (and_9_out, Register_for_A[3], not_2_out[3]);
  and and_10 (and_10_out, not_2_out[4], Register_for_A[4]);
  and and_11 (and_11_out, Register_for_B[0], not_3_out[0]);
  and and_12 (and_12_out, Register_for_B[1], not_3_out[1]);
  and and_13 (and_13_out, Register_for_B[2], not_3_out[2]);
  and and_14 (and_14_out, Register_for_B[3], not_3_out[3]);
  and and_15 (and_15_out, not_3_out[4], Register_for_B[4]);
  and and_16 (and_16_out, Register_for_B[0], not_4_out[0]);
  and and_17 (and_17_out, Register_for_B[1], not_4_out[1]);
  and and_18 (and_18_out, Register_for_B[2], not_4_out[2]);
  and and_19 (and_19_out, Register_for_B[3], not_4_out[3]);
  and and_20 (and_20_out, not_4_out[4], Register_for_B[4]);
  Multiplexer #(.select(2), .width(32), .enable("false")) multiplexer_1 (
    .in0(A_Current), .in1(Post_Mem_Value), .in2(Post_ALU_Value), .in3(Post_Mem_Value), .out(A),
    .sel(and_22_out));
  and and_21 (and_22_out[1], or_1_out, or_3_out);
  or or_3 (or_3_out, and_1_out, and_2_out, and_3_out, and_4_out, and_5_out);
  or or_4 (or_4_out, and_6_out, and_7_out, and_8_out, and_9_out, and_10_out);
  or or_5 (or_5_out, and_11_out, and_12_out, and_13_out, and_14_out, and_15_out);
  or or_6 (or_6_out, and_16_out, and_17_out, and_18_out, and_19_out, and_20_out);
  Multiplexer #(.select(2), .width(32), .enable("false")) multiplexer_2 (
    .in0(B_Current), .in1(Post_Mem_Value), .in2(Post_ALU_Value), .in3(Post_Mem_Value), .out(B),
    .sel(and_24_out));
  and and_22 (and_22_out[0], or_1_out, or_4_out);
  and and_23 (and_24_out[1], or_2_out, or_5_out);
  and and_24 (and_24_out[0], or_2_out, or_6_out);
endmodule

module _4 (
  input  [31:0] IN,
  output [31:0] OUT
);

  Adder #(.width(32)) adder_1 (.a(IN), .b(32'h4), .out(OUT), .cin(1'b0));  // open: cout
endmodule

module extend (
  input  extend_bits,
  input  [15:0] in_2,
  output [31:0] extended
);

  assign extended = {{16{extend_bits}}, in_2};  // Bit_Extender bit_extender_1
endmodule

module Decode (
  input  [31:0] INST,
  output [5:0] OP,
  output [4:0] W,
  output [4:0] A,
  output [4:0] B,
  output [4:0] SA,
  output [5:0] F
);


  assign A = INST[25:21];
  assign B = INST[20:16];
  assign F = INST[5:0];
  assign OP = INST[31:26];
  assign SA = INST[10:6];
  assign W = INST[15:11];
endmodule

module Memory2 (
  input  [31:0] D,
  input  [31:0] M,
  input  [5:0] OP,
  input  CLOCK,
  output [31:0] M_2
);

  // MIPS_RAM mips_ram_1: pin names not known; wires that end beside it: OP, D[19:0], M, CLOCK, M_2
endmodule

module IF_ID (
  input  [31:0] INST,
  input  [31:0] PC,
  input  CLOCK,
  output [31:0] INST_2,
  output [31:0] PC_2
);

  Register #(.width(32)) register_1 (.D(INST), .Q(INST_2), .clk(CLOCK));  // open: en, clr
  Register #(.width(32)) register_2 (.D(PC), .Q(PC_2), .clk(CLOCK));  // open: en, clr
endmodule

module ID_EX (
  input  [31:0] A,
  input  [31:0] B,
  input  [31:0] IMM,
  input  [5:0] OP,
  input  [4:0] RW,
  input  [4:0] RA,
  input  [4:0] RB,
  input  [4:0] SA,
  input  [5:0] F,
  input  [31:0] PC,
  input  CLOCK,
  output [31:0] A_2,
  output [31:0] B_2,
  output [31:0] IMM_2,
  output [5:0] OP_2,
  output [4:0] RW_2,
  output [4:0] RA_2,
  output [4:0] RB_2,
  output [4:0] SA_2,
  output [5:0] F_2,
  output [31:0] PC_2
);

  Register #(.width(32)) register_1 (.D(A), .Q(A_2), .clk(CLOCK));  // open: en, clr
  Register #(.width(32)) register_2 (.D(B), .Q(B_2), .clk(CLOCK));  // open: en, clr
  Register #(.width(32)) register_3 (.D(IMM), .Q(IMM_2), .clk(CLOCK));  // open: en, clr
  Register #(.width(6)) register_4 (.D(OP), .Q(OP_2), .clk(CLOCK));  // open: en, clr
  Register #(.width(5)) register_5 (.D(RW), .Q(RW_2), .clk(CLOCK));  // open: en, clr
  Register #(.width(5)) register_6 (.D(RA), .Q(RA_2), .clk(CLOCK));  // open: en, clr
  Register #(.width(5)) register_7 (.D(RB), .Q(RB_2), .clk(CLOCK));  // open: en, clr
  Register #(.width(5)) register_8 (.D(SA), .Q(SA_2), .clk(CLOCK));  // open: en, clr
  Register #(.width(6)) register_9 (.D(F), .Q(F_2), .clk(CLOCK));  // open: en, clr
  Register #(.width(32)) register_10 (.D(PC), .Q(PC_2), .clk(CLOCK));  // open: en, clr
endmodule

module EX_MEM (
  input  [31:0] D,
  input  [31:0] M,
  input  [5:0] OP,
  input  [4:0] RW,
  input  [4:0] RA,
  input  [4:0] RB,
  input  CLOCK,
  output [31:0] D_2,
  output [31:0] M_2,
  output [5:0] OP_2,
  output [4:0] RW_2,
  output [4:0] RA_2,
  output [4:0] RB_2
);

  Register #(.width(32)) register_1 (.D(D), .Q(D_2), .clk(CLOCK));  // open: en, clr
  Register #(.width(32)) register_2 (.D(M), .Q(M_2), .clk(CLOCK));  // open: en, clr
  Register #(.width(6)) register_3 (.D(OP), .Q(OP_2), .clk(CLOCK));  // open: en, clr
  Register #(.width(5)) register_4 (.D(RW), .Q(RW_2), .clk(CLOCK));  // open: en, clr
  Register #(.width(5)) register_5 (.D(RA), .Q(RA_2), .clk(CLOCK));  // open: en, clr
  Register #(.width(5)) register_6 (.D(RB), .Q(RB_2), .clk(CLOCK));  // open: en, clr
endmodule

module MEM_WB (
  input  [31:0] D,
  input  [31:0] M,
  input  [5:0] OP,
  input  [4:0] RW,
  input  CLOCK,
  output [31:0] D_2,
  output [31:0] M_2,
  output [5:0] OP_2,
  output [4:0] RW_2
);

  Register #(.width(32)) register_1 (.D(D), .Q(D_2), .clk(CLOCK));  // open: en, clr
  Register #(.width(32)) register_2 (.D(M), .Q(M_2), .clk(CLOCK));  // open: en, clr
  Register #(.width(6)) register_3 (.D(OP), .Q(OP_2), .clk(CLOCK));  // open: en, clr
  Register #(.width(5)) register_4 (.D(RW), .Q(RW_2), .clk(CLOCK));  // open: en, clr
endmodule

module ALUDecode (
  input  [5:0] F,
  input  [5:0] Op,
  output [3:0] ALU_Code,
  output IM,
  output out_5
);

  wire nand_1_out, nor_2_out, not_1_out;
  wire [0:0] and_1_out;
  wire [3:0] bit_extender_1_out, multiplexer_2_out, multiplexer_3_out, multiplexer_4_out;
  wire [5:0] multiplexer_1_out;

  Multiplexer #(.width(6), .enable("false")) multiplexer_1 (.in0(F), .in1(Op), .out(multiplexer_1_out), .sel(IM));
  or or_1 (IM, Op[0], Op[1], Op[2], Op[3], Op[4], Op[5]);
  nand nand_1 (nand_1_out, Op[0], Op[1], Op[2], Op[3]);
  assign bit_extender_1_out = {{3{nand_1_out}}, nand_1_out};  // Bit_Extender bit_extender_1
  nor nor_1 (out_5, IM, ~multiplexer_1_out[3], multiplexer_1_out[5]);  // NOR_Gate
  not not_1 (not_1_out, multiplexer_1_out[3]);
  Multiplexer #(.width(4), .enable("false")) multiplexer_2 (
    .in0({multiplexer_1_out[3:2], multiplexer_1_out[0], multiplexer_1_out[1]}),
    .in1({multiplexer_1_out[3], multiplexer_1_out[1], multiplexer_1_out[3], multiplexer_1_out[0]}),
    .out(multiplexer_2_out), .sel(not_1_out));
  and and_1 (and_1_out[0], multiplexer_1_out[1], ~multiplexer_1_out[2], multiplexer_1_out[3]);  // AND_Gate
  Multiplexer #(.width(4), .enable("false")) multiplexer_3 (
    .in0({multiplexer_1_out[2:0], and_1_out[0]}), .in1({and_1_out[0], multiplexer_1_out[3:1]}),
    .out(multiplexer_3_out), .sel(and_1_out[0]));
  nor nor_2 (nor_2_out, multiplexer_1_out[5], IM);
  Multiplexer #(.width(4), .enable("false")) multiplexer_4 (
    .in0(multiplexer_3_out), .in1(multiplexer_2_out), .out(multiplexer_4_out), .sel(nor_2_out));
  assign ALU_Code = multiplexer_4_out & bit_extender_1_out;  // AND_Gate and_2, 4 bits wide
endmodule
